// Logisim project ALU.circ as structural Verilog: 2 circuits, main circuit main
module main (
  input  [2:0] ALUOp,
  input  [15:0] A,
  input  [15:0] B,
  output [15:0] Result,
  output [15:0] Result2,
  output GT,
  output Zero,
  output LT
);

  wire [3:0] bit_extender_1_out;
  wire [15:0] adder_1_out, and_1_p3, and_1_p4, divider_1_out, divider_1_rem, multiplier_1_cout,
       multiplier_1_out, nor_1_out, shifter_1_out, shifter_2_out, subtractor_1_out;

  Bit_Extender #(.in_width(16), .out_width(4)) bit_extender_1 (.in(B), .out(bit_extender_1_out));
  // AND_Gate #(.width(16)) and_1: pin names not known; wires that end beside it: A, B, and_1_p3, and_1_p4
  assign nor_1_out = ~(and_1_p3 | A | B);  // NOR_Gate nor_1, 16 bits wide
  Adder #(.width(16)) adder_1 (.a(A), .b(B), .out(adder_1_out));  // open: cin, cout
  Subtractor #(.width(16)) subtractor_1 (.a(A), .b(B), .out(subtractor_1_out));  // open: bin, bout
  Multiplier #(.width(16)) multiplier_1 (.a(A), .b(B), .out(multiplier_1_out), .cout(multiplier_1_cout));  // open: cin
  Divider #(.width(16)) divider_1 (.a(A), .b(B), .out(divider_1_out), .rem(divider_1_rem));  // open: upper
  Shifter #(.width(16)) shifter_1 (.in(A), .\dist (bit_extender_1_out), .out(shifter_1_out));
  Shifter #(.width(16), .shift("lr")) shifter_2 (.in(A), .\dist (bit_extender_1_out), .out(shifter_2_out));
  Comparator #(.width(16)) comparator_1 (.a(A), .b({16{1'b0}}), .gt(GT), .eq(Zero), .lt(LT));
  Multiplexer #(.select(3), .width(16)) multiplexer_1 (
    .in0(and_1_p4), .in1(nor_1_out), .in2(adder_1_out), .in3(subtractor_1_out), .in4(multiplier_1_out),
    .in5(divider_1_out), .in6(shifter_1_out), .in7(shifter_2_out), .out(Result), .sel(ALUOp));  // open: en
  Multiplexer #(.select(3), .width(16)) multiplexer_2 (
    .in4(multiplier_1_cout), .in5(divider_1_rem), .out(Result2), .sel(ALUOp));  // open: in0, in1, in2, in3, in6, in7, en

  // Notes on the sheet:
  //   Thomas (Teddy) Potter - tep32
  //   Inputs
  //   Design your ALU in this file
  //   A - First ALU input
  //   B - Second ALU input
  //   Result - ALU main result
  //   ALUOp - The control signal defining the behaviour of the ALU
  //   Result2 - Output for MSB of mul/div operations
  //   GT/Zero/LT - Comparison of input A with zero
  //   Outputs
endmodule

module test (
  input  [2:0] in_1,
  input  [15:0] in_2,
  input  [15:0] in_3,
  output [15:0] out_4,
  output [15:0] out_5,
  output out_6,
  output out_7,
  output out_8
);

  main main_1 (.ALUOp(in_1), .A(in_2), .B(in_3), .Result(out_4), .GT(out_6), .Zero(out_7), .LT(out_8), .Result2(out_5));

  // Notes on the sheet:
  //   Test your circuit!
endmodule
