// Logisim project RegFile.circ as structural Verilog: 2 circuits, main circuit main
module main (
  input  [15:0] WriteData0,
  input  [15:0] WriteData1,
  input  [2:0] WriteSelect0,
  input  [2:0] ReadSelect0,
  input  [2:0] ReadSelect1,
  input  WE0,
  input  WE1,
  input  Clock,
  output [15:0] Reg0,
  output [15:0] Reg1,
  output [15:0] Reg2,
  output [15:0] Reg3,
  output [15:0] Reg4,
  output [15:0] Reg5,
  output [15:0] Reg6,
  output [15:0] Reg7,
  output [15:0] ReadData0,
  output [15:0] ReadData1
);

  wire or_2_out, or_4_out, or_6_out, or_8_out, or_10_out, or_12_out, or_14_out, or_16_out, WE0Reg0, WE0Reg1,
       WE0Reg2, WE0Reg3, WE0Reg4, WE0Reg5, WE0Reg6, WE0Reg7, WE1Reg0, WE1Reg1, WE1Reg2, WE1Reg3, WE1Reg4,
       WE1Reg5, WE1Reg6, WE1Reg7;
  wire [2:0] adder_1_out, adder_2_out;
  wire [15:0] Data0Reg0, Data0Reg1, Data0Reg2, Data0Reg3, Data0Reg4, Data0Reg5, Data0Reg6, Data0Reg7,
       Data1Reg0, Data1Reg1, Data1Reg2, Data1Reg3, Data1Reg4, Data1Reg5, Data1Reg6, Data1Reg7, or_1_out,
       or_3_out, or_5_out, or_7_out, or_9_out, or_11_out, or_13_out, or_15_out, undriven, undriven_2,
       undriven_3, undriven_4, undriven_5, undriven_6, undriven_7, undriven_8;

  Demultiplexer #(.select(3)) demultiplexer_1 (
    .out0(WE0Reg0), .out1(WE0Reg1), .out2(WE0Reg2), .out3(WE0Reg3), .out4(WE0Reg4), .out5(WE0Reg5),
    .out6(WE0Reg6), .out7(WE0Reg7), .in(WE0), .sel(WriteSelect0));  // open: en
  Demultiplexer #(.select(3)) demultiplexer_2 (
    .out0(WE1Reg0), .out1(WE1Reg1), .out2(WE1Reg2), .out3(WE1Reg3), .out4(WE1Reg4), .out5(WE1Reg5),
    .out6(WE1Reg6), .out7(WE1Reg7), .in(WE1), .sel(adder_1_out));  // open: en
  Adder #(.width(3)) adder_1 (.a(WriteSelect0), .b(3'b001), .out(adder_1_out));  // open: cin, cout
  assign or_1_out = Data0Reg0 | Data1Reg0 | undriven;  // OR_Gate or_1, 16 bits wide
  or or_2 (or_2_out, undriven[0], WE0Reg0, WE1Reg0);
  assign or_3_out = Data0Reg1 | Data1Reg1 | undriven_2;  // OR_Gate or_3, 16 bits wide
  or or_4 (or_4_out, undriven_2[0], WE0Reg1, WE1Reg1);
  assign or_5_out = Data0Reg2 | Data1Reg2 | undriven_3;  // OR_Gate or_5, 16 bits wide
  or or_6 (or_6_out, undriven_3[0], WE0Reg2, WE1Reg2);
  assign or_7_out = Data0Reg3 | Data1Reg3 | undriven_4;  // OR_Gate or_7, 16 bits wide
  or or_8 (or_8_out, undriven_4[0], WE0Reg3, WE1Reg3);
  Register #(.width(16)) u_Reg0 (.D(or_1_out), .en(or_2_out), .Q(Reg0), .clk(Clock));  // open: clr
  Register #(.width(16)) u_Reg1 (.D(or_3_out), .en(or_4_out), .Q(Reg1), .clk(Clock));  // open: clr
  Register #(.width(16)) u_Reg2 (.D(or_5_out), .en(or_6_out), .Q(Reg2), .clk(Clock));  // open: clr
  Register #(.width(16)) u_Reg3 (.D(or_7_out), .en(or_8_out), .Q(Reg3), .clk(Clock));  // open: clr
  Demultiplexer #(.select(3), .width(16)) demultiplexer_3 (
    .out0(Data0Reg0), .out1(Data0Reg1), .out2(Data0Reg2), .out3(Data0Reg3), .out4(Data0Reg4),
    .out5(Data0Reg5), .out6(Data0Reg6), .out7(Data0Reg7), .in(WriteData0), .sel(WriteSelect0));  // open: en
  assign or_9_out = Data0Reg4 | Data1Reg4 | undriven_5;  // OR_Gate or_9, 16 bits wide
  or or_10 (or_10_out, undriven_5[0], WE0Reg4, WE1Reg4);
  assign or_11_out = Data0Reg5 | Data1Reg5 | undriven_6;  // OR_Gate or_11, 16 bits wide
  or or_12 (or_12_out, undriven_6[0], WE0Reg5, WE1Reg5);
  assign or_13_out = Data0Reg6 | Data1Reg6 | undriven_7;  // OR_Gate or_13, 16 bits wide
  or or_14 (or_14_out, undriven_7[0], WE0Reg6, WE1Reg6);
  assign or_15_out = Data0Reg7 | Data1Reg7 | undriven_8;  // OR_Gate or_15, 16 bits wide
  or or_16 (or_16_out, undriven_8[0], WE0Reg7, WE1Reg7);
  Register #(.width(16)) u_Reg4 (.D(or_9_out), .en(or_10_out), .Q(Reg4), .clk(Clock));  // open: clr
  Register #(.width(16)) u_Reg5 (.D(or_11_out), .en(or_12_out), .Q(Reg5), .clk(Clock));  // open: clr
  Register #(.width(16)) u_Reg6 (.D(or_13_out), .en(or_14_out), .Q(Reg6), .clk(Clock));  // open: clr
  Register #(.width(16)) u_Reg7 (.D(or_15_out), .en(or_16_out), .Q(Reg7), .clk(Clock));  // open: clr
  Demultiplexer #(.select(3), .width(16)) demultiplexer_4 (
    .out0(Data1Reg0), .out1(Data1Reg1), .out2(Data1Reg2), .out3(Data1Reg3), .out4(Data1Reg4),
    .out5(Data1Reg5), .out6(Data1Reg6), .out7(Data1Reg7), .in(WriteData1), .sel(adder_2_out));  // open: en
  Adder #(.width(3)) adder_2 (.a(WriteSelect0), .b(3'b001), .out(adder_2_out));  // open: cin, cout
  Multiplexer #(.select(3), .width(16)) multiplexer_1 (
    .in0(Reg0), .in1(Reg1), .in2(Reg2), .in3(Reg3), .in4(Reg4), .in5(Reg5), .in6(Reg6), .in7(Reg7),
    .out(ReadData0), .sel(ReadSelect0));  // open: en
  Multiplexer #(.select(3), .width(16)) multiplexer_2 (
    .in0(Reg0), .in1(Reg1), .in2(Reg2), .in3(Reg3), .in4(Reg4), .in5(Reg5), .in6(Reg6), .in7(Reg7),
    .out(ReadData1), .sel(ReadSelect1));  // open: en
  // Pins of 1 and 16 bits meet at undriven_8
  // Pins of 1 and 16 bits meet at undriven_4
  // Pins of 1 and 16 bits meet at undriven_7
  // Pins of 1 and 16 bits meet at undriven
  // Pins of 1 and 16 bits meet at undriven_5
  // Pins of 1 and 16 bits meet at undriven_2
  // Pins of 1 and 16 bits meet at undriven_3
  // Pins of 1 and 16 bits meet at undriven_6

  // Other names for the same wires on the sheet: WriteEnable0 = WE0; WriteEnable1 = WE1

  // Notes on the sheet:
  //   Inputs
  //   Thomas (Teddy) Potter - tep32
  //   Add the registers to this file
  //   WriteSelect0 - Register to write to
  //   WE0 - Enable writing to 1 register
  //   ReadSelect0 - First register to read data from
  //   ReadSelect1 - Second register to read data from
  //   WE1 - Enable writing to 2nd register (mul/div)
  //   ReadData0 - Data being read from first register
  //   ReadData1 - Data being read from second register
  //   WriteData0 - The data to be written to register by most instructions
  //   WriteData1 - The data to be written to second register by mul/div
  //   These can be used for debug and testing
  //   and design the logic to control them
  //   Outputs
endmodule

module test (
  input  [15:0] Write_data_A,
  input  Write_Enable_Port_A,
  input  [2:0] in_3,
  input  [15:0] Write_data_B,
  input  Write_Enable_Port_B,
  input  [2:0] Select_Read_A,
  input  [2:0] Select_Read_B
);

  wire Clock_out;
  wire [15:0] main_1_readdata0, main_1_readdata1, main_1_reg0, main_1_reg1, main_1_reg2, main_1_reg3,
       main_1_reg4, main_1_reg5, main_1_reg6, main_1_reg7;

  // Probe on main_1_reg0
  // Probe on main_1_reg1
  // Probe on main_1_reg2
  // Probe on main_1_reg3
  Button Clock (.out(Clock_out));
  // Probe on main_1_reg4
  // Probe on main_1_reg5
  // Probe on main_1_reg6
  // Probe on main_1_reg7
  main main_1 (
    .WriteData0(Write_data_A), .WriteData1(Write_data_B), .ReadData0(main_1_readdata0),
    .ReadData1(main_1_readdata1), .WriteSelect0(in_3), .ReadSelect0(Select_Read_A),
    .ReadSelect1(Select_Read_B), .Reg0(main_1_reg0), .Reg1(main_1_reg1), .Reg2(main_1_reg2),
    .Reg3(main_1_reg3), .Reg4(main_1_reg4), .Reg5(main_1_reg5), .Reg6(main_1_reg6), .Reg7(main_1_reg7),
    .WE0(Write_Enable_Port_A), .WE1(Write_Enable_Port_B), .Clock(Clock_out));
  // Probe on main_1_readdata0
  // Probe on main_1_readdata1

  // Notes on the sheet:
  //   Test your circuit!
endmodule
