// Logisim project umips.circ as structural Verilog: 3 circuits, main circuit main
module main (
  output [15:0] Reg0,
  output [15:0] Reg1,
  output [15:0] Reg2,
  output [15:0] Reg3,
  output [15:0] Reg4,
  output [15:0] Reg5,
  output [15:0] Reg6,
  output [15:0] Reg7,
  output [3:0] Output3,
  output [3:0] Output2,
  output [3:0] Output1,
  output [3:0] Output0,
  output halt
);

  wire ALUSrc, and_1_out, and_2_out, branch, Clock, Fields_subop, jalSelect, jrSelect, jump, liControl,
       main_2_gt, main_2_lt, main_2_zero, MemRead, MemtoReg, MemWrite, multiplexer_5_out, not_1_p2,
       not_2_out, not_3_p2, or_1_out, or_3_out, put, RegWrite, SignedUnsigned, WriteB;
  wire [1:0] BranchSelect;
  wire [2:0] ALUOp, Fields_rs;
  wire [3:0] Fields_opcode;
  wire [7:0] adder_1_out, bit_extender_2_out, DataB, demultiplexer_1_out1, demultiplexer_2_out0,
       demultiplexer_2_out1, Fields_immediate_rt, jalData, multiplexer_1_out, multiplexer_2_out,
       Program_Counter_q;
  wire [15:0] beep, bit_extender_1_out, bit_extender_3_out, DataA, liData, main_1_readdata1, main_2_result,
       main_2_result2, multiplexer_3_out, multiplexer_4_out, or_4_out, ram_1_data, rom_1_data, WriteData;

  Adder adder_1 (.a(Program_Counter_q), .b(8'h1), .out(adder_1_out));  // open: cin, cout
  Demultiplexer #(.width(8)) demultiplexer_1 (
    .out0(jalData), .out1(demultiplexer_1_out1), .in(adder_1_out), .sel(not_1_p2));  // open: en
  // NOT_Gate not_1: pin names not known; wires that end beside it: jalSelect, not_1_p2
  Multiplexer #(.width(8)) multiplexer_1 (
    .in0(demultiplexer_1_out1), .in1(multiplexer_2_out), .out(multiplexer_1_out), .sel(or_1_out));  // open: en
  or or_1 (or_1_out, and_2_out, jump);
  Register Program_Counter (.D(multiplexer_1_out), .en(and_1_out), .Q(Program_Counter_q), .clk(Clock));  // open: clr
  and and_1 (and_1_out, 1'b1, not_2_out);
  not not_2 (not_2_out, halt);
  assign bit_extender_1_out = {{8{1'b0}}, jalData};  // Bit_Extender bit_extender_1
  Clock clock_1 (.out(Clock));
  assign beep = WriteData | bit_extender_1_out;  // OR_Gate or_2, 16 bits wide
  ROM #(.dataWidth(16)) rom_1 (.addr(Program_Counter_q), .data(rom_1_data), .sel(1'b1));
  Control control_1 (
    .Opcode(Fields_opcode), .Subop(Fields_subop), .ALUOp(ALUOp), .MemtoReg(MemtoReg), .WriteB(WriteB),
    .MemRead(MemRead), .BranchSelect(BranchSelect), .MemWrite(MemWrite), .liControl(liControl),
    .RegWrite(RegWrite), .ALUSrc(ALUSrc), .halt(halt), .put(put), .SignedUnsigned(SignedUnsigned),
    .jump(jump), .branch(branch), .jalSelect(jalSelect), .jrSelect(jrSelect));
  Fields Fields (
    .Instruction(rom_1_data), .Subop(Fields_subop), .Immediate_Rt(Fields_immediate_rt), .Rs(Fields_rs),
    .Opcode(Fields_opcode));
  Multiplexer #(.width(8)) multiplexer_2 (
    .in0(Fields_immediate_rt), .in1(bit_extender_2_out), .out(multiplexer_2_out), .sel(jrSelect));  // open: en
  Bit_Extender #(.in_width(16), .out_width(8)) bit_extender_2 (.in(DataA), .out(bit_extender_2_out));
  Multiplexer #(.width(16)) multiplexer_3 (
    .in0(beep), .in1(liData), .out(multiplexer_3_out), .sel(liControl));  // open: en
  Demultiplexer #(.width(8)) demultiplexer_2 (
    .out0(demultiplexer_2_out0), .out1(demultiplexer_2_out1), .in(Fields_immediate_rt), .sel(or_3_out));  // open: en
  or or_3 (or_3_out, liControl, SignedUnsigned, SignedUnsigned);
  RegFile_main main_1 (
    .WriteData0(multiplexer_3_out), .WriteData1(main_2_result2), .ReadData0(DataA),
    .ReadData1(main_1_readdata1), .WriteSelect0(Fields_rs), .ReadSelect0(Fields_rs),
    .ReadSelect1(Fields_immediate_rt[7:5]), .Reg0(Reg0), .Reg1(Reg1), .Reg2(Reg2), .Reg3(Reg3), .Reg4(Reg4),
    .Reg5(Reg5), .Reg6(Reg6), .Reg7(Reg7), .WE0(RegWrite), .WE1(WriteB), .Clock(Clock));
  assign bit_extender_3_out = {{8{demultiplexer_2_out0[7]}}, demultiplexer_2_out0};  // Bit_Extender bit_extender_3
  assign liData = {{8{1'b0}}, demultiplexer_2_out1};  // Bit_Extender bit_extender_4
  ALU_main main_2 (
    .ALUOp(ALUOp), .A(DataA), .B(multiplexer_4_out), .Result(main_2_result), .GT(main_2_gt),
    .Zero(main_2_zero), .LT(main_2_lt), .Result2(main_2_result2));
  Multiplexer #(.width(16)) multiplexer_4 (
    .in0(main_1_readdata1), .in1(or_4_out), .out(multiplexer_4_out), .sel(ALUSrc));  // open: en
  Bit_Extender #(.in_width(16), .out_width(8)) bit_extender_5 (.in(main_1_readdata1), .out(DataB));
  assign or_4_out = bit_extender_3_out | liData;  // OR_Gate or_4, 16 bits wide
  Register #(.width(16)) register_1 (
    .D(DataA), .en(put), .Q({Output3, Output2, Output1, Output0}), .clk(Clock));  // open: clr
  and and_2 (and_2_out, multiplexer_5_out, branch);
  // NOT_Gate not_3: pin names not known; wires that end beside it: main_2_zero, not_3_p2
  Multiplexer #(.select(2)) multiplexer_5 (
    .in0(main_2_gt), .in1(main_2_lt), .in2(not_3_p2), .in3(main_2_zero), .out(multiplexer_5_out),
    .sel(BranchSelect));  // open: en
  Hex_Digit_Display hex_digit_display_1 (.value(Output3));  // open: dp
  Hex_Digit_Display hex_digit_display_2 (.value(Output2));  // open: dp
  RAM #(.dataWidth(16), .bus("separate")) ram_1 (
    .addr(DataB), .din(DataA), .data(ram_1_data), .str(MemWrite), .sel(1'b1), .clk(Clock), .ld(MemRead));  // open: clr
  Hex_Digit_Display hex_digit_display_3 (.value(Output1));  // open: dp
  Hex_Digit_Display hex_digit_display_4 (.value(Output0));  // open: dp
  Multiplexer #(.width(16)) multiplexer_6 (
    .in0(main_2_result), .in1(ram_1_data), .out(WriteData), .sel(MemtoReg));  // open: en

  // Notes on the sheet:
  //   Thomas (Teddy) Potter - tep32
  //    Don't modify these, they are used for debug and testing
endmodule

module Fields (
  input  [15:0] Instruction,
  output Subop,
  output [7:0] Immediate_Rt,
  output [2:0] Rs,
  output [3:0] Opcode
);


  assign Immediate_Rt = Instruction[8:1];
  assign Opcode = Instruction[15:12];
  assign Rs = Instruction[11:9];
  assign Subop = Instruction[0];
endmodule

module Control (
  input  [3:0] Opcode,
  input  Subop,
  output [2:0] ALUOp,
  output MemtoReg,
  output WriteB,
  output MemRead,
  output [1:0] BranchSelect,
  output MemWrite,
  output liControl,
  output RegWrite,
  output ALUSrc,
  output halt,
  output put,
  output SignedUnsigned,
  output jump,
  output branch,
  output jalSelect,
  output jrSelect
);

  wire ADD, ADDI, ADDUI, AND, bn, bp, bx, bz, decoder_1_out0, decoder_1_out1, decoder_1_out2, decoder_1_out3,
       decoder_1_out6, decoder_1_out7, DIV, j, MUL, NOR, not_1_p2, or_1_out, or_2_out, or_3_out, or_5_out,
       SLL, SRL, SUB;

  Decoder #(.select(4)) decoder_1 (
    .out0(decoder_1_out0), .out1(decoder_1_out1), .out2(decoder_1_out2), .out3(decoder_1_out3), .out4(bp),
    .out5(liControl), .out6(decoder_1_out6), .out7(decoder_1_out7), .out8(put), .out9(halt),
    .out10(jalSelect), .out11(j), .out12(bn), .out13(bx), .out14(jrSelect), .out15(bz), .sel(Opcode));  // open: en
  Demultiplexer demultiplexer_1 (.out0(ADD), .out1(SUB), .in(decoder_1_out0), .sel(Subop));  // open: en
  Demultiplexer demultiplexer_2 (.out0(NOR), .out1(AND), .in(decoder_1_out1), .sel(Subop));  // open: en
  Demultiplexer demultiplexer_3 (.out0(MUL), .out1(DIV), .in(decoder_1_out2), .sel(Subop));  // open: en
  Demultiplexer demultiplexer_4 (.out0(ADDUI), .out1(ADDI), .in(decoder_1_out3), .sel(Subop));  // open: en
  Demultiplexer demultiplexer_5 (.out0(SRL), .out1(SLL), .in(decoder_1_out6), .sel(Subop));  // open: en
  Demultiplexer demultiplexer_6 (.out0(MemWrite), .out1(MemtoReg), .in(decoder_1_out7), .sel(Subop));  // open: en
  or or_1 (or_1_out, 1'b1, bp);
  Priority_Encoder #(.select(2)) priority_encoder_1 (
    .in0(or_1_out), .in1(bn), .in2(bx), .in3(bz), .out(BranchSelect));  // open: gs, en_out, en_in
  // NOT_Gate not_1: pin names not known; wires that end beside it: ADDUI, not_1_p2
  or or_2 (or_2_out, ADD, ADDI, ADDUI, bp, bn, bx, bz, jalSelect);
  or or_3 (or_3_out, ADDI, not_1_p2);
  // NOT_Gate not_2: pin names not known; wires that end beside it: or_3_out, SignedUnsigned
  or or_4 (branch, bp, bn, bx, bz);
  or or_5 (or_5_out, 1'b1, MemtoReg, MemWrite);
  or or_6 (MemRead, MemtoReg, MemWrite);
  Priority_Encoder priority_encoder_2 (
    .in0(or_5_out), .in1(NOR), .in2(or_2_out), .in3(SUB), .in4(MUL), .in5(DIV), .in6(SLL), .in7(SRL),
    .out(ALUOp));  // open: en_in, gs, en_out
  or or_7 (ALUSrc, ADDI, bp, bn, bx, bz, ADDUI);
  or or_8 (jump, jrSelect, j, jalSelect);
  or or_9 (WriteB, MUL, DIV);
  or or_10 (RegWrite, ADD, SUB, AND, NOR, ADDUI, ADDI, MUL, DIV, SLL, SRL, MemtoReg, liControl, jalSelect);

  // Other names for the same wires on the sheet: jal = jalSelect; jr = jrSelect; li = liControl; lw = MemtoReg;
  //   sw = MemWrite
endmodule
